# Fritzing sketch avrbreakout_display (saved by Fritzing 0.9.1b)
breadboards: 2

parts:
  Explore_AVR_Breakout_Board1 = Explore AVR Breakout Board
  CP1 = Explore USB to UART [package="DIP (Dual Inline) [THT]"]
  Q1 = NPN-Transistor [package="TO92 [THT]"]
  R1 = Resistor [tolerance=±5% resistance=220 package=THT]  # not connected
  R2 = Resistor [tolerance=±5% resistance=220 package=THT]
  7_Segment1 = 7 Segment Display

nets:
  N1: Explore_AVR_Breakout_Board1.PIN3, 7_Segment1.Segment_A
  N2: Explore_AVR_Breakout_Board1.pin_4, 7_Segment1.Segment_B
  N3: Explore_AVR_Breakout_Board1.pin_5, 7_Segment1.Segment_C
  N4: Explore_AVR_Breakout_Board1.pin_6, 7_Segment1.Segment_D
  N5: Explore_AVR_Breakout_Board1.pin_7, 7_Segment1.Segment_E
  N6: Explore_AVR_Breakout_Board1.pin_8, 7_Segment1.Segment_F
  N7: Explore_AVR_Breakout_Board1.pin_9, 7_Segment1.Segment_G
  N8: Explore_AVR_Breakout_Board1.pin_10, 7_Segment1.Segment_DP
  N9: Explore_AVR_Breakout_Board1.pin_40, R2.Pin_0
  N10: Explore_AVR_Breakout_Board1.pin_41, CP1.pin1
  N11: Explore_AVR_Breakout_Board1.pin_42, CP1.pin2
  N12: Explore_AVR_Breakout_Board1.pin_43, CP1.pin3
  N13: Explore_AVR_Breakout_Board1.pin_44, CP1.pin4
  N14: Explore_AVR_Breakout_Board1.pin_45, CP1.pin5
  N15: Explore_AVR_Breakout_Board1.pin_46, CP1.pin6
  N16: Explore_AVR_Breakout_Board1.pin_47, CP1.pin7
  N17: Q1.E, R2.Pin_1
  N18: Q1.C, 7_Segment1.common_anode
