# Fritzing sketch avrbreakout_lcd (saved by Fritzing 0.9.1b)
breadboards: 2

parts:
  Explore_AVR_Breakout_Board1 = Explore AVR Breakout Board
  CP1 = Explore USB to UART [package="DIP (Dual Inline) [THT]"]
  Breakout1 = LCD breakout [package="DIP (Dual Inline) [THT]"]
  LCD1 = LCD screen  # not connected

nets:
  N1: Explore_AVR_Breakout_Board1.PIN3, Breakout1.pin1
  N2: Explore_AVR_Breakout_Board1.pin_4, Breakout1.pin2
  N3: Explore_AVR_Breakout_Board1.pin_5, Breakout1.pin3
  N4: Explore_AVR_Breakout_Board1.pin_25, Breakout1.pin8
  N5: Explore_AVR_Breakout_Board1.pin_26, Breakout1.pin_9
  N6: Explore_AVR_Breakout_Board1.pin_27, Breakout1.pin_10
  N7: Explore_AVR_Breakout_Board1.pin_28, Breakout1.pin_11
  N8: Explore_AVR_Breakout_Board1.pin_39, Breakout1.pin_14
  N9: Explore_AVR_Breakout_Board1.pin_40, Breakout1.pin_15
  N10: Explore_AVR_Breakout_Board1.pin_41, CP1.pin1
  N11: Explore_AVR_Breakout_Board1.pin_42, CP1.pin2
  N12: Explore_AVR_Breakout_Board1.pin_43, CP1.pin3
  N13: Explore_AVR_Breakout_Board1.pin_44, CP1.pin4
  N14: Explore_AVR_Breakout_Board1.pin_45, CP1.pin5
  N15: Explore_AVR_Breakout_Board1.pin_46, CP1.pin6
  N16: Explore_AVR_Breakout_Board1.pin_47, CP1.pin7
  N17: Breakout1.pin_17, Breakout1.pin_18, Breakout1.pin_19, Breakout1.pin_20, Breakout1.pin_21, Breakout1.pin_23, Breakout1.pin_24, Breakout1.pin_25, Breakout1.pin_26, Breakout1.pin_27, Breakout1.pin_29, Breakout1.pin_30, Breakout1.pin_31, Breakout1.pin_32, Breakout1.pin_33, Breakout1.pin_35
