# Fritzing sketch avrbreakout_setup (saved by Fritzing 0.9.1b)
breadboards: 2

parts:
  Explore_AVR_Breakout_Board1 = Explore AVR Breakout Board
  CP1 = Explore USB to UART [package="DIP (Dual Inline) [THT]"]

nets:
  N1: Explore_AVR_Breakout_Board1.pin_41, CP1.pin1
  N2: Explore_AVR_Breakout_Board1.pin_42, CP1.pin2
  N3: Explore_AVR_Breakout_Board1.pin_43, CP1.pin3
  N4: Explore_AVR_Breakout_Board1.pin_44, CP1.pin4
  N5: Explore_AVR_Breakout_Board1.pin_45, CP1.pin5
  N6: Explore_AVR_Breakout_Board1.pin_46, CP1.pin6
  N7: Explore_AVR_Breakout_Board1.pin_47, CP1.pin7
