# Fritzing sketch avrbreakout_switch (saved by Fritzing 0.9.1b)
breadboards: 2

parts:
  Explore_AVR_Breakout_Board1 = Explore AVR Breakout Board
  CP1 = Explore USB to UART [package="DIP (Dual Inline) [THT]"]
  R1 = Resistor [tolerance=±5% resistance=220 package=THT]
  LED1 = LED - 5mm [color="Red (633nm)" package="5 mm [THT]"]
  S1 = Pushbutton [package="[THT]"]
  R2 = Resistor [tolerance=±5% resistance=220 package=THT]

nets:
  N1: Explore_AVR_Breakout_Board1.PIN3, LED1.anode
  N2: Explore_AVR_Breakout_Board1.pin_21, S1.Pin_1, S1.Pin_2, R2.Pin_0
  N3: Explore_AVR_Breakout_Board1.pin_39, R1.Pin_1, S1.Pin_3, S1.Pin_4
  N4: Explore_AVR_Breakout_Board1.pin_40, R2.Pin_1
  N5: Explore_AVR_Breakout_Board1.pin_41, CP1.pin1
  N6: Explore_AVR_Breakout_Board1.pin_42, CP1.pin2
  N7: Explore_AVR_Breakout_Board1.pin_43, CP1.pin3
  N8: Explore_AVR_Breakout_Board1.pin_44, CP1.pin4
  N9: Explore_AVR_Breakout_Board1.pin_45, CP1.pin5
  N10: Explore_AVR_Breakout_Board1.pin_46, CP1.pin6
  N11: Explore_AVR_Breakout_Board1.pin_47, CP1.pin7
  N12: R1.Pin_0, LED1.cathode
